// Logisim project SR.circ as structural Verilog: 1 circuit, main circuit main
module main (
  input  D0,
  input  D1
);

  wire clock_1_out, multiplexer_1_out, multiplexer_2_out, multiplexer_3_out, multiplexer_4_out,
       multiplexer_5_out, multiplexer_6_out, multiplexer_7_out, multiplexer_8_out;

  Clock clock_1 (.out(clock_1_out));
  Multiplexer #(.enable("false")) multiplexer_1 (.in0(D0), .out(multiplexer_1_out));  // open: in1, sel
  D_Flip_Flop d_ff_1 (.clk(clock_1_out), .D(multiplexer_1_out));  // open: Q, Qn, preset, en, reset
  Multiplexer #(.enable("false")) multiplexer_2 (.in0(D1), .out(multiplexer_2_out));  // open: in1, sel
  D_Flip_Flop d_ff_2 (.clk(clock_1_out), .D(multiplexer_2_out));  // open: Q, Qn, preset, en, reset
  Multiplexer #(.enable("false")) multiplexer_3 (.out(multiplexer_3_out));  // open: in0, in1, sel
  D_Flip_Flop d_ff_3 (.clk(clock_1_out), .D(multiplexer_3_out));  // open: Q, Qn, preset, en, reset
  Multiplexer #(.enable("false")) multiplexer_4 (.out(multiplexer_4_out));  // open: in0, in1, sel
  D_Flip_Flop d_ff_4 (.clk(clock_1_out), .D(multiplexer_4_out));  // open: Q, Qn, preset, en, reset
  Multiplexer #(.enable("false")) multiplexer_5 (.out(multiplexer_5_out));  // open: in0, in1, sel
  D_Flip_Flop d_ff_5 (.clk(clock_1_out), .D(multiplexer_5_out));  // open: Q, Qn, preset, en, reset
  Multiplexer #(.enable("false")) multiplexer_6 (.out(multiplexer_6_out));  // open: in0, in1, sel
  D_Flip_Flop d_ff_6 (.clk(clock_1_out), .D(multiplexer_6_out));  // open: Q, Qn, preset, en, reset
  Multiplexer #(.enable("false")) multiplexer_7 (.out(multiplexer_7_out));  // open: in0, in1, sel
  D_Flip_Flop d_ff_7 (.clk(clock_1_out), .D(multiplexer_7_out));  // open: Q, Qn, preset, en, reset
  Multiplexer #(.enable("false")) multiplexer_8 (.out(multiplexer_8_out));  // open: in0, in1, sel
  D_Flip_Flop d_ff_8 (.clk(clock_1_out), .D(multiplexer_8_out));  // open: Q, Qn, preset, en, reset
endmodule
